# Fritzing sketch Score_Board (saved by Fritzing 0.9.2b)
circuit board: 8.46667cm x 5.64444cm
breadboards: 2

parts:
  Part1 = Arduino Uno (Rev3)
  BAT1 = BC9VPC [package=bc9vpc]
  C4 = Capacitor Polarized [package=panasonic_c]
  IC3 = Voltage Regulator [package=78xxl]
  C5 = Capacitor Polarized [package=panasonic_c]
  U1 = 74HC595 [package="DIP16 [THT]"]
  U2 = 74HC595 [package="DIP16 [THT]"]
  7_Segment1 = 7 Segment Display
  7_Segment2 = 7 Segment Display
  S1 = Pushbutton [package="[SMD]"]
  S2 = Pushbutton [package="[SMD]"]
  S3 = Pushbutton [package="[SMD]"]
  R6 = Resistor [tolerance=±5% resistance=470 package=THT]
  R7 = Resistor [tolerance=±5% resistance=470 package=THT]
  R8 = Resistor [tolerance=±5% resistance=470 package=THT]

nets:
  N1: Part1.D8, S3.Pin_1, S3.Pin_2, R8.Pin_0
  N2: Part1.D9_PWM, S2.Pin_1, S2.Pin_2, R7.Pin_0
  N3: Part1.D10_PWM/SS, S1.Pin_1, S1.Pin_2, R6.Pin_0
  N4: Part1.D2, U1.DS
  N5: Part1.D3_PWM, U1.ST_CP, U2.ST_CP
  N6: Part1.D4, U1.SH_CP, U2.SH_CP
  N7: Part1.5V, S1.Pin_3, S1.Pin_4, S2.Pin_3, S2.Pin_4, S3.Pin_3, S3.Pin_4
  N8: Part1.GND, R6.Pin_1, R7.Pin_1, R8.Pin_1
  N9: BAT1.V+, C4.+, IC3.IN
  GND: BAT1.V-, C4.-, IC3.GND, C5.-, U1.GND, U1.OE, U2.GND, U2.OE, 7_Segment1.common_cathode, 7_Segment2.common_cathode
  VCC: IC3.OUT, C5.+, U1.MR, U1.VCC, U2.MR, U2.VCC
  N10: U1.Q1, 7_Segment1.Segment_A
  N11: U1.Q2, 7_Segment1.Segment_B
  N12: U1.Q3, 7_Segment1.Segment_C
  N13: U1.Q4, 7_Segment1.Segment_D
  N14: U1.Q5, 7_Segment1.Segment_E
  N15: U1.Q6, 7_Segment1.Segment_F
  N16: U1.Q7, 7_Segment1.Segment_G
  N17: U1.Q7', U2.DS
  N18: U2.Q1, 7_Segment2.Segment_A
  N19: U2.Q2, 7_Segment2.Segment_B
  N20: U2.Q3, 7_Segment2.Segment_C
  N21: U2.Q4, 7_Segment2.Segment_D
  N22: U2.Q5, 7_Segment2.Segment_E
  N23: U2.Q6, 7_Segment2.Segment_F
  N24: U2.Q7, 7_Segment2.Segment_G

// code stored in the sketch: ScoreDisplay0_3.ino
// Pin out variables
const int dataPin = 2;
const int latchPin = 3;
const int clockPin = 4;
const int scoreUpPin = 10;
const int scoreDownPin = 9;
const int scoreResetPin = 8;

// Button states variables
int buttonUpState = LOW;
int lastButtonUpState = LOW;
int buttonDownState = LOW;
int lastButtonDownState = LOW;
int buttonResetState = LOW;
int lastButtonResetState = LOW;
int buttonUpRead = LOW;
int buttonDownRead = LOW;
int buttonResetRead = LOW;
// Button read variables

// Debounce variables
long lastUpDebounceTime = 0;  // the last time the output pin was toggled
long lastDownDebounceTime = 0;  // the last time the output pin was toggled
long lastResetDebounceTime = 0;  // the last time the output pin was toggled
long debounceDelay = 50;    // the debounce time; increase if the output flickers

// Display variables
int score = 0;
int numberDisplay[10] = {126, 48, 109, 121, 51, 91, 95, 112, 127, 115};

void setup() {
  Serial.begin(9600);
  pinMode(dataPin, OUTPUT);
  pinMode(latchPin, OUTPUT);
  pinMode(clockPin, OUTPUT);
  pinMode(scoreUpPin, INPUT);
  pinMode(scoreDownPin, INPUT);
  pinMode(scoreResetPin, INPUT);
  updateDisplay(0);
}

void loop(){

  // Read in button values
  buttonUpRead = digitalRead(scoreUpPin);
  buttonDownRead = digitalRead(scoreDownPin);
  buttonResetRead = digitalRead(scoreResetPin);
  
  // Check if debounce timer variables need to be updated
  debounceUpdate();
 
  checkUpButton();
  checkDownButton();
  checkResetButton();
  
  lastButtonUpState = buttonUpRead;
  lastButtonDownState = buttonDownRead;
  lastButtonResetState = buttonResetRead;
}  
  
void updateCount(char* action, char* reset){   
  if (reset == "y"){
    score = 0;
  }
  else{   
    if (action == "+"){
      score++;
      if (score > 9){
        score = 0;
      }
    }else{
      score--;
      if (score < 0){
        score = 0;
      }
    }
  }
  updateDisplay(score);
//  delay(100);
}

void updateDisplay(int value){
  digitalWrite(latchPin, LOW);
  shiftOut(dataPin, clockPin, LSBFIRST, numberDisplay[value]);
  digitalWrite(latchPin, HIGH);
}

void debounceUpdate(){
  if (buttonUpRead != lastButtonUpState) {
    // set new debounce time.
    lastUpDebounceTime = millis();
  }
  
  if (buttonDownRead != lastButtonDownState) {
    // set new debounce time.
    lastDownDebounceTime = millis();
  }
  
  if (buttonResetRead != lastButtonResetState) {
    // set new debounce time.
    lastResetDebounceTime = millis();
  }
}

void checkUpButton(){
  // If the time the program has been running - the time the button was pressed is greater than the debounceDelay
  // ie. if the time since last press is > than the debouceDelay
  if ((millis() - lastUpDebounceTime) > debounceDelay) {
    // if the button has changed from the state:
    if (buttonUpRead != buttonUpState) {
      // Change the buttonState Variable
      buttonUpState = buttonUpRead;
      // if the button state has gone from low to high then button has been pressed.
      if (buttonUpState == HIGH) {
        updateCount("+","n");
      }
    }
  }
}

void checkDownButton(){
  // If the time the program has been running - the time the button was pressed is greater than the debounceDelay
  // ie. if the time since last press is > than the debouceDelay
  if ((millis() - lastDownDebounceTime) > debounceDelay) {
  // if the button state has changed:
    if (buttonDownRead != buttonDownState) {
      // Change the buttonState Variable
      buttonDownState = buttonDownRead;
      // if button state has gone from low to high it has been pressed.
      if (buttonDownState == HIGH) {
        updateCount("-","n");
      }
    }
  }
}

void checkResetButton(){
  // If the time the program has been running - the time the button was pressed is greater than the debounceDelay
  // ie. if the time since last press is > than the debouceDelay
  if ((millis() - lastResetDebounceTime) > debounceDelay) {
  // if the button state has changed:
    if (buttonResetRead != buttonResetState) {
      // Change the buttonState Variable
      buttonResetState = buttonResetRead;
      // if button state has gone from low to high it has been pressed.
      if (buttonResetState == HIGH) {
        updateCount("+","y");
      }
    }
  }
}
/* 
  for (int currentValue = 0; currentValue <= 9; currentValue ++){
  
  // Disable the latch whil we clock in data
  digitalWrite(latchPin, LOW);
  
  // Send the value as a binary sequence to the module
  shiftOut(dataPin, clockPin, LSBFIRST, numberDisplay[currentValue]);
  
  // Enable the latch again to set the output states
  digitalWrite(latchPin, HIGH);
  
  delay(1000);
  }
 */
